// Digital circuit simulator.dig as structural Verilog
module simulator (
  input  [8:0] entrada,
  output D,
  output A,
  output C,
  output B
);

  nome #(.applicationType("GHDL")) u_nome (.entrada(entrada), .D(D), .C(C), .B(B), .A(A));
endmodule

/* Test case test:
entrada D C B A
0x1FE 1 1 1 0
0x1FC 1 1 0 1
0X1F8 1 1 0 0
0X1F0 1 0 1 1
0X1E0 1 0 1 0
0X1C0 1 0 0 1
0X180 1 0 0 0
0X100 0 1 1 1
0x1ff 1 1 1 1
*/

/* Code of nome:
library IEEE;
use IEEE.std_logic_1164.all;


entity nome is
port(
entrada : in std_logic_vector ( 8 downto 0 );
D,C,B,A : out std_logic
);
end nome;

architecture expressao of nome is 
begin
process(entrada)
begin
    
    D <= '0' when entrada(8) = '0' else
        '0' when entrada(7) = '0' else
        '1' when entrada(6) = '0' else
        '1' when entrada(5) = '0' else
        '1' when entrada(4) = '0' else
        '1' when entrada(3) = '0' else
        '1' when entrada(2) = '0' else
        '1' when entrada(1) = '0' else
        '1' when entrada(0) = '0' else
	'1' when entrada = "111111111";

    C <= '1' when entrada(8) = '0' else
        '1' when entrada(7) = '0' else
        '0' when entrada(6) = '0' else
        '0' when entrada(5) = '0' else
        '0' when entrada(4) = '0' else
        '0' when entrada(3) = '0' else
        '1' when entrada(2) = '0' else
        '1' when entrada(1) = '0' else
        '1' when entrada(0) = '0' else
	'1' when entrada = "111111111";
    B <= '1' when entrada(8) = '0' else
        '1' when entrada(7) = '0' else
        '0' when entrada(6) = '0' else
        '0' when entrada(5) = '0' else
        '1' when entrada(4) = '0' else
        '1' when entrada(3) = '0' else
        '0' when entrada(2) = '0' else
        '0' when entrada(1) = '0' else
        '1' when entrada(0) = '0' else
	'1' when entrada = "111111111";
    A <= '0' when entrada(8) = '0' else
        '1' when entrada(7) = '0' else
        '0' when entrada(6) = '0' else
        '1' when entrada(5) = '0' else
        '0' when entrada(4) = '0' else
        '1' when entrada(3) = '0' else
        '0' when entrada(2) = '0' else
        '1' when entrada(1) = '0' else
        '0' when entrada(0) = '0' else
	'1' when entrada = "111111111";
end process;
end expressao;
*/
