// Digital circuit simulator.dig as structural Verilog
module simulator (
  input  [5:0] ativar,
  output Y0,
  output Y1,
  output Y2,
  output Y3,
  output Y4,
  output Y5,
  output Y6,
  output Y7
);

  nome #(.applicationType("GHDL")) u_nome (
    .ativar(ativar), .y0(Y0), .y1(Y1), .y2(Y2), .y3(Y3), .y4(Y4), .y5(Y5), .y6(Y6), .y7(Y7));
endmodule

/* Test case Test:
ativar Y0 Y1 Y2 Y3 Y4 Y5 Y6 Y7
0x2F 1 1 1 1 1 1 1 1
0x10 0 1 1 1 1 1 1 1
0x11 1 0 1 1 1 1 1 1
0x12 1 1 0 1 1 1 1 1
0x13 1 1 1 0 1 1 1 1
0x14 1 1 1 1 0 1 1 1
0x15 1 1 1 1 1 0 1 1
0x16 1 1 1 1 1 1 0 1
0x17 1 1 1 1 1 1 1 0
*/

/* Code of nome:
library IEEE;
use IEEE.std_logic_1164.all;


entity nome is
port(
ativar : in std_logic_vector ( 5 downto 0 );
-- GL = ativar(0)
-- g1 = ativar(1)
-- g2 = ativar (2)
y0,y1,y2,y3,y4,y5,y6,y7 : out std_logic
);
end nome;

architecture nome_da_archi of nome is
begin
process(ativar)
begin
if ativar(2) = '1' then 
y0<='1';y1<='1';y2<='1';y3<='1';y4<='1';y5<='1';y6<='1';y7<='1';
end if;
if ativar(1) = '0' then y0<='1';y1<='1';y2<='1';y3<='1';y4<='1';y5<='1';y6<='1';y7<='1';end if;
if ativar = "010000" then y0<='0';y1<='1';y2<='1';y3<='1';y4<='1';y5<='1';y6<='1';y7<='1';end if;
if ativar = "010001" then y0<='1';y1<='0';y2<='1';y3<='1';y4<='1';y5<='1';y6<='1';y7<='1';end if;
if ativar = "010010" then y0<='1';y1<='1';y2<='0';y3<='1';y4<='1';y5<='1';y6<='1';y7<='1';end if;
if ativar = "010011" then y0<='1';y1<='1';y2<='1';y3<='0';y4<='1';y5<='1';y6<='1';y7<='1';end if;
if ativar = "010100" then y0<='1';y1<='1';y2<='1';y3<='1';y4<='0';y5<='1';y6<='1';y7<='1';end if;
if ativar = "010101" then y0<='1';y1<='1';y2<='1';y3<='1';y4<='1';y5<='0';y6<='1';y7<='1';end if;
if ativar = "010110" then y0<='1';y1<='1';y2<='1';y3<='1';y4<='1';y5<='1';y6<='0';y7<='1';end if;
if ativar = "010111" then y0<='1';y1<='1';y2<='1';y3<='1';y4<='1';y5<='1';y6<='1';y7<='0';end if;



end process;
end nome_da_archi;
*/
