// Digital circuit circuit.dig as structural Verilog
module circuit (
  input  OE,
  input  [2:0] selects,
  input  [7:0] position,
  output z,
  output z_2
);

  main #(.applicationType("GHDL")) u_main (
    .OE(OE), .selects(selects), .position_switch(position), .z(z), .z_invert(z_2));
endmodule

/* Test case:
OE selects position z |z
0 0b101 0b10111010 0 0
*/

/* Code of main:
library IEEE;
use IEEE.std_logic_1164.all;

entity main is
port(
	OE : in std_logic;
	selects : in std_logic_vector ( 2 downto 0 );
	position_switch : in std_logic_vector ( 7 downto 0 );
	z : out std_logic;
	z_invert : out std_logic
);
end main;

architecture main_arch of main is
begin
process(OE, selects,position_switch)
begin
if not OE = '1' then
	if selects = "---" then
		z <= 'Z';
		z_invert <= 'Z';
	end if;
end if;
if not OE = '0' then
	if selects = "000" then
		z <= position_switch(0);
		z_invert <= not position_switch(0);
	elsif selects = "001" then
		z <= position_switch(1);
		z_invert <= not position_switch(1);
	elsif selects = "010" then
		z <= position_switch(2);
		z_invert <= not position_switch(2);
	elsif selects = "011" then
		z <= position_switch(3);
		z_invert <= not position_switch(3);
	elsif selects = "100" then
		z <= position_switch(4);
		z_invert <= not position_switch(4);
	elsif selects = "101" then
		z <= position_switch(5);
		z_invert <= not position_switch(5);
	elsif selects = "110" then
		z <= position_switch(6);
		z_invert <= not position_switch(6);
	elsif selects = "111" then
		z <= position_switch(7);
		z_invert <= not position_switch(7);
	end if;
end if;
end process;
end main_arch;
*/
